# Fritzing sketch connection-diagram (saved by Fritzing 0.9.2b)
circuit board: 3.98313cm x 5.52369cm
breadboards: 1

parts:
  Bauteil1 = Arduino Nano (Rev3.0)
  M1 = Stepper Motor - Bipolar
  S1 = Pushbutton [package=THT]
  J2 = female pin header, 2 pins [form="♀ (female)"]
  MD09B1 = A4988 Stepper Motor Driver Carrier
  R5 = Resistor [tolerance=±5% resistance=100 package=THT]
  R6 = Resistor [tolerance=±5% resistance=1k package=THT]
  R7 = Resistor [tolerance=±5% resistance=1k package=THT]
  R8 = Resistor [tolerance=±5% resistance=1k package=THT]
  R9 = Resistor [tolerance=±5% resistance=1k package=THT]
  V1 = DC Power [voltage=12V]  # not connected

nets (from the pcb view):
  N1: Bauteil1.RESET, R5.Pin_0
  N2: Bauteil1.GND, M1.D, R5.Pin_1, R6.Pin_1, R7.Pin_1, R8.Pin_1, R9.Pin_1
  N3: Bauteil1.D3, MD09B1.MS3
  N4: Bauteil1.D6, Bauteil1.D7, Bauteil1.D8, S1.leg0, S1.leg1, J2.pin1, J2.pin2, MD09B1.Enable
  VIN: Bauteil1.D9, Bauteil1.D10, Bauteil1.D11/MOSI, Bauteil1.D12/MISO, Bauteil1.VIN, MD09B1.VDD, R6.Pin_0, R7.Pin_0, R8.Pin_0, R9.Pin_0
  N5: Bauteil1.A2, MD09B1.SLEEP
  N6: Bauteil1.A1, MD09B1.STEP
  N7: Bauteil1.A0, MD09B1.DIR
  N8: M1.A, MD09B1.OUT_2B
  N9: M1.C, MD09B1.OUT_2A
  N10: M1.B, MD09B1.OUT_1A
  N11: MD09B1.MS2, MD09B1.GROUND, MD09B1.OUT_1B
